# Fritzing sketch Untitled Sketch 2.fzz anyu (saved by Fritzing 0.9.9b)
breadboards: 1

parts:
  Mod1 = Raspberry Pi 4B
  R1 = Resistor [tolerance=±5% power=0.25 resistance=10k package=THT]
  R2 = Resistor [tolerance=±5% power=0.25 resistance=3.3 package=THT]
  R3 = Resistor [tolerance=±5% power=0.25 resistance=3.3 package=THT]
  S1_fényerő_fel = Pushbutton [package="[THT]"]
  S2_fényero_le = Pushbutton [package="[THT]"]
  R4 = Resistor [tolerance=±5% power=0.25 resistance=10k package=THT]
  R5 = Resistor [tolerance=±5% power=0.25 resistance=3.3 package=THT]
  LED1 = LED - 5mm [color="Yellow (592nm)" current=0.030 package="5 mm [THT]"]
  R6 = Resistor [tolerance=±5% power=0.25 resistance=10k package=THT]
  R7 = Resistor [tolerance=±5% power=0.25 resistance=3.3 package=THT]
  S3_fényerő_ki-be = Pushbutton [package="[THT]"]

nets:
  N1: Mod1.3V3, R1.Pin_1, R4.Pin_1, R6.Pin_1
  N2: Mod1.GPIO14, R2.Pin_0
  N3: Mod1.GPIO15, R7.Pin_0
  N4: Mod1.GPIO18, R3.Pin_0
  N5: Mod1.GPIO24, R5.Pin_0
  N6: Mod1.GND, S1_fényerő_fel.Pin_1, S1_fényerő_fel.Pin_2, S2_fényero_le.Pin_1, S2_fényero_le.Pin_2, LED1.cathode, S3_fényerő_ki-be.Pin_1, S3_fényerő_ki-be.Pin_2
  N7: R1.Pin_0, R2.Pin_1, S1_fényerő_fel.Pin_3, S1_fényerő_fel.Pin_4
  N8: R3.Pin_1, S2_fényero_le.Pin_3, S2_fényero_le.Pin_4, R4.Pin_0
  N9: R5.Pin_1, LED1.anode
  N10: R6.Pin_0, R7.Pin_1, S3_fényerő_ki-be.Pin_3, S3_fényerő_ki-be.Pin_4
